# Fritzing sketch voltage (saved by Fritzing 0.7.12b)
breadboards: 1

parts:
  Max1 = chipKIT Max32 [chip_label=IC package="SIP (Single Inline) [THT]"]
  R1 = Resistor [tolerance=±5% resistance=4.7k package=THT]
  R2 = Resistor [tolerance=±5% resistance=1k package=THT]
  R3 = Resistor [tolerance=±5% resistance=330 package=THT]

nets:
  N1: Max1.A0, R1.Pin_0, R2.Pin_1
  N2: Max1.GND, R3.Pin_0
  N3: R2.Pin_0, R3.Pin_1

notes:
  Vin+
  Vin-GROUND

custom parts:
  chipKIT Max32: chipKIT's Max32
